// Logisim project hw1.circ as structural Verilog: 3 circuits, main circuit my hw1 circuit
module my_hw1_circuit (
  input  a,
  input  b,
  input  c,
  output x,
  output y
);

  wire nand_1_out, nand_2_out, or_1_out;

  nand nand_1 (nand_1_out, a, b);
  or or_1 (or_1_out, b, c);
  nand nand_2 (nand_2_out, nand_1_out, c);
  not not_1 (y, or_1_out);
  xor xor_1 (x, nand_2_out, y);
endmodule

module minimized (
  input  a,
  input  b,
  input  c,
  output x,
  output y
);

  wire nand_1_out, nand_2_out, nor_2_out;

  nand nand_1 (nand_1_out, a, b);
  nor nor_1 (y, b, c);
  nand nand_2 (nand_2_out, nand_1_out, c);
  nor nor_2 (nor_2_out, b, c);
  xor xor_1 (x, nand_2_out, nor_2_out);
endmodule

module product_of_sums (
  input  a,
  input  b,
  input  c,
  output x,
  output y
);

  wire not_1_out, or_1_out;

  not not_1 (not_1_out, c);
  or or_1 (or_1_out, a, not_1_out);
  nor nor_1 (y, b, c);
  and and_1 (x, b, or_1_out);
endmodule
