// Logisim project hammingTest.circ as structural Verilog: 1 circuit, main circuit main
// rP1
module main (
  input  rP0,
  input  cP0,
  input  rP1,
  input  cp1,
  input  d1,
  output out_6
);

  wire and_1_out, xor_1_out, xor_2_out;

  xor xor_1 (xor_1_out, rP0, cP0);
  xor xor_2 (xor_2_out, rP1, cp1);
  and and_1 (and_1_out, xor_1_out, xor_2_out);
  xor xor_3 (out_6, and_1_out, d1);
endmodule
