// Logisim project Ring6Led.circ as structural Verilog: 2 circuits, main circuit main
module main (
);

  wire clock_1_out, d_ff_1_q, d_ff_2_q, d_ff_3_q;

  Clock clock_1 (.out(clock_1_out));
  D_Flip_Flop d_ff_1 (.clk(clock_1_out), .D(d_ff_3_q), .Q(d_ff_1_q));  // open: Qn, preset, en, reset
  D_Flip_Flop d_ff_2 (.clk(clock_1_out), .D(d_ff_1_q), .Q(d_ff_2_q));  // open: Qn, preset, en, reset
  D_Flip_Flop d_ff_3 (.clk(clock_1_out), .D(d_ff_2_q), .Q(d_ff_3_q));  // open: Qn, preset, en, reset
endmodule

module Ring (
  input  A,
  input  B,
  input  C,
  output a_2,
  output b_2,
  output c_2,
  output y1,
  output y2,
  output y3,
  output y4,
  output y5,
  output y6
);

  wire and_3_out, and_4_out, and_7_out, and_10_out, not_1_out, not_2_out, not_3_out, not_4_out, not_5_out,
       not_6_out, not_7_out, not_8_out, not_9_out, not_10_out, not_11_out, not_12_out;

  not not_1 (not_1_out, A);
  not not_2 (not_2_out, B);
  not not_3 (not_3_out, B);
  not not_4 (not_4_out, B);
  not not_5 (not_5_out, C);
  not not_6 (not_6_out, A);
  not not_7 (not_7_out, B);
  not not_8 (not_8_out, A);
  not not_9 (not_9_out, A);
  not not_10 (not_10_out, B);
  and and_1 (y5, A, C);
  and and_2 (y6, A, B);
  and and_3 (and_3_out, not_1_out, B);
  and and_4 (and_4_out, A, not_2_out);
  and and_5 (b_2, not_3_out, C);
  and and_6 (c_2, not_4_out, not_5_out);
  and and_7 (and_7_out, not_6_out, not_7_out);
  not not_11 (not_11_out, C);
  and and_8 (y2, not_8_out, C);
  and and_9 (y3, not_9_out, B);
  and and_10 (and_10_out, A, not_10_out);
  not not_12 (not_12_out, C);
  or or_1 (a_2, and_3_out, and_4_out);
  and and_11 (y1, and_7_out, not_11_out);
  and and_12 (y4, and_10_out, not_12_out);
endmodule
