// Logisim project Ring6Led2.circ as structural Verilog: 3 circuits, main circuit main
module main (
  output out_1,
  output out_2,
  output out_3,
  output out_4,
  output out_5,
  output out_6
);

  wire clock_1_out, d_ff_1_q, d_ff_2_q, d_ff_3_q, ring2_1_a_2, ring2_1_b_2, ring2_1_c_2;

  Clock clock_1 (.out(clock_1_out));
  Ring2 ring2_1 (
    .A(d_ff_1_q), .B(d_ff_2_q), .C(d_ff_3_q), .a_2(ring2_1_a_2), .b_2(ring2_1_b_2), .c_2(ring2_1_c_2),
    .y1(out_1), .y2(out_2), .y3(out_3), .y4(out_4), .y5(out_5), .y6(out_6));
  D_Flip_Flop d_ff_1 (.clk(clock_1_out), .D(ring2_1_a_2), .Q(d_ff_1_q));  // open: Qn, preset, en, reset
  D_Flip_Flop d_ff_2 (.clk(clock_1_out), .D(ring2_1_b_2), .Q(d_ff_2_q));  // open: Qn, preset, en, reset
  D_Flip_Flop d_ff_3 (.clk(clock_1_out), .D(ring2_1_c_2), .Q(d_ff_3_q));  // open: Qn, preset, en, reset
endmodule

module Ring (
  input  A,
  input  B,
  input  C,
  output a_2,
  output b_2,
  output c_2,
  output y1,
  output y2,
  output y3,
  output y4,
  output y5,
  output y6
);

  wire and_3_out, and_4_out, and_7_out, and_10_out, not_1_out, not_2_out, not_3_out, not_4_out, not_5_out,
       not_6_out, not_7_out, not_8_out, not_9_out, not_10_out, not_11_out, not_12_out;

  not not_1 (not_1_out, A);
  not not_2 (not_2_out, B);
  not not_3 (not_3_out, B);
  not not_4 (not_4_out, B);
  not not_5 (not_5_out, C);
  not not_6 (not_6_out, A);
  not not_7 (not_7_out, B);
  not not_8 (not_8_out, A);
  not not_9 (not_9_out, A);
  not not_10 (not_10_out, B);
  and and_1 (y5, A, C);
  and and_2 (y6, A, B);
  and and_3 (and_3_out, not_1_out, B);
  and and_4 (and_4_out, A, not_2_out);
  and and_5 (b_2, not_3_out, C);
  and and_6 (c_2, not_4_out, not_5_out);
  and and_7 (and_7_out, not_6_out, not_7_out);
  not not_11 (not_11_out, C);
  and and_8 (y2, not_8_out, C);
  and and_9 (y3, not_9_out, B);
  and and_10 (and_10_out, A, not_10_out);
  not not_12 (not_12_out, C);
  or or_1 (a_2, and_3_out, and_4_out);
  and and_11 (y1, and_7_out, not_11_out);
  and and_12 (y4, and_10_out, not_12_out);
endmodule

module Ring2 (
  input  A,
  input  B,
  input  C,
  output a_2,
  output b_2,
  output c_2,
  output y1,
  output y2,
  output y3,
  output y4,
  output y5,
  output y6
);

  wire and_1_out, and_2_out, and_3_out, and_4_out, and_5_out, and_6_out, and_7_out, and_8_out, and_9_out,
       and_11_out, and_12_out, and_13_out, and_14_out, not_1_out, not_2_out, not_3_out, not_4_out, not_5_out,
       not_6_out, not_7_out, not_8_out, not_9_out, not_10_out, not_11_out, not_12_out, not_13_out,
       not_14_out, not_15_out;

  not not_1 (not_1_out, A);
  not not_2 (not_2_out, B);
  not not_3 (not_3_out, B);
  not not_4 (not_4_out, C);
  not not_5 (not_5_out, A);
  not not_6 (not_6_out, B);
  not not_7 (not_7_out, C);
  not not_8 (not_8_out, A);
  not not_9 (not_9_out, B);
  not not_10 (not_10_out, A);
  not not_11 (not_11_out, A);
  not not_12 (not_12_out, A);
  not not_13 (not_13_out, B);
  not not_14 (not_14_out, C);
  not not_15 (not_15_out, B);
  and and_1 (and_1_out, A, C);
  and and_2 (and_2_out, A, B);
  and and_3 (and_3_out, not_1_out, B);
  and and_4 (and_4_out, A, not_2_out);
  and and_5 (and_5_out, A, C);
  and and_6 (and_6_out, not_3_out, not_4_out);
  and and_7 (and_7_out, B, C);
  and and_8 (and_8_out, not_5_out, not_6_out, not_7_out);
  and and_9 (and_9_out, A, B);
  and and_10 (y2, not_8_out, not_9_out);
  and and_11 (and_11_out, not_10_out, C);
  and and_12 (and_12_out, not_11_out, B);
  and and_13 (and_13_out, not_12_out, B);
  and and_14 (and_14_out, A, not_13_out, not_14_out);
  and and_15 (y5, A, not_15_out);
  or or_1 (y6, and_1_out, and_2_out);
  or or_2 (a_2, and_3_out, and_4_out, and_5_out);
  or or_3 (c_2, and_6_out, and_7_out);
  or or_4 (y1, and_8_out, and_9_out);
  or or_5 (y3, and_11_out, and_12_out);
  or or_6 (y4, and_13_out, and_14_out);

  assign b_2 = C;
endmodule
