// Logisim project RingAll.circ as structural Verilog: 4 circuits, main circuit main
module main (
);

  wire clock_1_out, d_ff_1_q, d_ff_2_q, d_ff_3_q;

  Clock clock_1 (.out(clock_1_out));
  D_Flip_Flop d_ff_1 (.clk(clock_1_out), .D(d_ff_3_q), .Q(d_ff_1_q));  // open: Qn, preset, en, reset
  D_Flip_Flop d_ff_2 (.clk(clock_1_out), .D(d_ff_1_q), .Q(d_ff_2_q));  // open: Qn, preset, en, reset
  D_Flip_Flop d_ff_3 (.clk(clock_1_out), .D(d_ff_2_q), .Q(d_ff_3_q));  // open: Qn, preset, en, reset
endmodule

module Ring (
  input  A,
  input  B,
  input  C,
  output a_2,
  output b_2,
  output c_2,
  output y1,
  output y2,
  output y3,
  output y4,
  output y5,
  output y6
);

  wire and_3_out, and_4_out, and_7_out, and_10_out, not_1_out, not_2_out, not_3_out, not_4_out, not_5_out,
       not_6_out, not_7_out, not_8_out, not_9_out, not_10_out, not_11_out, not_12_out;

  not not_1 (not_1_out, A);
  not not_2 (not_2_out, B);
  not not_3 (not_3_out, B);
  not not_4 (not_4_out, B);
  not not_5 (not_5_out, C);
  not not_6 (not_6_out, A);
  not not_7 (not_7_out, B);
  not not_8 (not_8_out, A);
  not not_9 (not_9_out, A);
  not not_10 (not_10_out, B);
  and and_1 (y5, A, C);
  and and_2 (y6, A, B);
  and and_3 (and_3_out, not_1_out, B);
  and and_4 (and_4_out, A, not_2_out);
  and and_5 (b_2, not_3_out, C);
  and and_6 (c_2, not_4_out, not_5_out);
  and and_7 (and_7_out, not_6_out, not_7_out);
  not not_11 (not_11_out, C);
  and and_8 (y2, not_8_out, C);
  and and_9 (y3, not_9_out, B);
  and and_10 (and_10_out, A, not_10_out);
  not not_12 (not_12_out, C);
  or or_1 (a_2, and_3_out, and_4_out);
  and and_11 (y1, and_7_out, not_11_out);
  and and_12 (y4, and_10_out, not_12_out);
endmodule

module bal (
  output out_1,
  output out_2,
  output out_3,
  output out_4,
  output out_5,
  output out_6
);

  wire clock_1_out, d_ff_1_q, d_ff_2_q, d_ff_3_q, newring_1_x, newring_1_y, newring_1_z;

  newring newring_1 (
    .A(d_ff_1_q), .B(d_ff_2_q), .C(d_ff_3_q), .x(newring_1_x), .y(newring_1_y), .z(newring_1_z), .u(out_1),
    .v(out_2), .w(out_3), .s(out_4), .t(out_5), .x2(out_6));
  Clock clock_1 (.out(clock_1_out));
  D_Flip_Flop d_ff_1 (.clk(clock_1_out), .D(newring_1_x), .Q(d_ff_1_q));  // open: Qn, preset, en, reset
  D_Flip_Flop d_ff_2 (.clk(clock_1_out), .D(newring_1_y), .Q(d_ff_2_q));  // open: Qn, preset, en, reset
  D_Flip_Flop d_ff_3 (.clk(clock_1_out), .D(newring_1_z), .Q(d_ff_3_q));  // open: Qn, preset, en, reset
endmodule

module newring (
  input  A,
  input  B,
  input  C,
  output x,
  output y,
  output z,
  output u,
  output v,
  output w,
  output s,
  output t,
  output x2
);

  wire and_1_out, and_2_out, and_3_out, and_6_out, and_8_out, and_9_out, and_10_out, and_12_out, and_13_out,
       and_14_out, and_15_out, and_16_out, and_17_out, not_1_out, not_2_out, not_3_out, not_4_out, not_5_out,
       not_6_out, not_7_out, not_8_out, not_9_out, not_10_out, not_11_out, not_12_out, not_13_out,
       not_14_out, not_15_out, not_16_out, not_17_out;

  not not_1 (not_1_out, A);
  not not_2 (not_2_out, B);
  not not_3 (not_3_out, B);
  not not_4 (not_4_out, C);
  not not_5 (not_5_out, A);
  not not_6 (not_6_out, B);
  not not_7 (not_7_out, A);
  not not_8 (not_8_out, B);
  not not_9 (not_9_out, A);
  not not_10 (not_10_out, A);
  not not_11 (not_11_out, B);
  not not_12 (not_12_out, B);
  and and_1 (and_1_out, A, C);
  and and_2 (and_2_out, A, B);
  and and_3 (and_3_out, not_1_out, B);
  not not_13 (not_13_out, C);
  not not_14 (not_14_out, B);
  and and_4 (y, not_2_out, C);
  and and_5 (z, not_3_out, not_4_out);
  and and_6 (and_6_out, not_5_out, not_6_out);
  not not_15 (not_15_out, C);
  and and_7 (v, not_7_out, not_8_out);
  and and_8 (and_8_out, not_9_out, C);
  and and_9 (and_9_out, not_10_out, B);
  not not_16 (not_16_out, A);
  and and_10 (and_10_out, A, not_11_out);
  not not_17 (not_17_out, C);
  and and_11 (t, A, not_12_out);
  or or_1 (x2, and_1_out, and_2_out);
  and and_12 (and_12_out, and_3_out, not_13_out);
  and and_13 (and_13_out, A, not_14_out);
  and and_14 (and_14_out, and_6_out, not_15_out);
  and and_15 (and_15_out, A, B);
  or or_2 (w, and_8_out, and_9_out);
  and and_16 (and_16_out, not_16_out, B);
  and and_17 (and_17_out, and_10_out, not_17_out);
  or or_3 (x, and_12_out, and_13_out);
  or or_4 (u, and_14_out, and_15_out);
  or or_5 (s, and_16_out, and_17_out);
endmodule
