// Logisim project c11-JKCounterMod6.circ as structural Verilog: 1 circuit, main circuit main
module main (
  input  in_1,
  output out_2,
  output out_3,
  output out_4
);

  wire and_1_out, j_k_ff_1_qn, j_k_ff_2_qn, j_k_ff_3_qn;

  and and_1 (and_1_out, out_4, out_3);
  J_K_Flip_Flop j_k_ff_1 (
    .J(and_1_out), .clk(in_1), .K(j_k_ff_2_qn), .Q(out_2), .Qn(j_k_ff_1_qn));  // open: preset, en, reset
  J_K_Flip_Flop j_k_ff_2 (
    .J(j_k_ff_3_qn), .clk(in_1), .K(out_2), .Q(out_3), .Qn(j_k_ff_2_qn));  // open: preset, en, reset
  J_K_Flip_Flop j_k_ff_3 (
    .J(out_3), .clk(in_1), .K(j_k_ff_1_qn), .Q(out_4), .Qn(j_k_ff_3_qn));  // open: preset, en, reset
endmodule
