// Logisim project c8-Mod4.circ as structural Verilog: 1 circuit, main circuit main
module main (
  input  in_1,
  output out_2,
  output out_3,
  output out_4,
  output out_5
);

  D_Flip_Flop d_ff_1 (.clk(in_1), .D(out_5), .Q(out_2));  // open: Qn, preset, en, reset
  D_Flip_Flop d_ff_2 (.clk(in_1), .D(out_2), .Q(out_3));  // open: Qn, preset, en, reset
  D_Flip_Flop d_ff_3 (.clk(in_1), .D(out_3), .Q(out_4));  // open: Qn, preset, en, reset
  D_Flip_Flop d_ff_4 (.clk(in_1), .D(out_4), .Q(out_5));  // open: Qn, preset, en, reset
endmodule
