// Logisim project mod 6 counter with mux.circ as structural Verilog
module mux (
  input  q1,
  input  q2,
  input  q3,
  output Q1_2,
  output Q2_2,
  output Q3_2
);

  wire [2:0] combo_2_1_s0;

  combo_2 combo_2_1 (.q1(q1), .q2(q2), .q3(q3), .s0(combo_2_1_s0[0]), .s1(combo_2_1_s0[1]), .s2(combo_2_1_s0[2]));
  Multiplexer #(.select(3)) multiplexer_1 (
    .in0(1'b0), .in1(1'b0), .in2(1'b1), .in3(1'b1), .in4(1'b1), .in5(1'b1), .in6(1'b0), .in7(1'b0),
    .out(Q1_2), .sel(combo_2_1_s0));  // open: en
  Multiplexer #(.select(3)) multiplexer_2 (
    .in0(1'b0), .in1(1'b1), .in2(1'b1), .in3(1'b1), .in4(1'b1), .in5(1'b0), .in6(1'b0), .in7(1'b0),
    .out(Q2_2), .sel(combo_2_1_s0));  // open: en
  Multiplexer #(.select(3)) multiplexer_3 (
    .in0(1'b1), .in1(1'b1), .in2(1'b1), .in3(1'b0), .in4(1'b0), .in5(1'b0), .in6(1'b0), .in7(1'b1),
    .out(Q3_2), .sel(combo_2_1_s0));  // open: en
endmodule

module combo_2 (
  input  q1,
  input  q2,
  input  q3,
  output s0,
  output s1,
  output s2
);

  wire nand_1_out, nand_2_out, nand_3_out, nand_4_out, nand_5_out, nand_7_out, nand_8_out, nand_9_out,
       nand_10_out, nand_11_out;

  nand nand_1 (nand_1_out, q1, q1);
  nand nand_2 (nand_2_out, q2, q2);
  nand nand_3 (nand_3_out, q3, q3);
  nand nand_4 (nand_4_out, q2, q2);
  nand nand_5 (nand_5_out, q3, q3);
  nand nand_6 (s2, q3, q3);
  nand nand_7 (nand_7_out, nand_1_out, nand_2_out, nand_3_out);
  nand nand_8 (nand_8_out, q1, q3);
  nand nand_9 (nand_9_out, q1, q2);
  nand nand_10 (nand_10_out, nand_4_out, nand_5_out);
  nand nand_11 (nand_11_out, q2, q3);
  nand nand_12 (s0, nand_7_out, nand_8_out, nand_9_out);
  nand nand_13 (s1, nand_10_out, nand_11_out);
endmodule

module main (
  input  q1,
  input  q2,
  input  q3,
  output Q3_2,
  output Q2_2,
  output Q1_2
);

  wire clock_1_out, mux_1_q1_2, mux_1_q2_2, mux_1_q3_2;

  mux mux_1 (.q1(q1), .q2(q2), .q3(q3), .Q1_2(mux_1_q1_2), .Q2_2(mux_1_q2_2), .Q3_2(mux_1_q3_2));
  Clock clock_1 (.out(clock_1_out));
  D_Flip_Flop d_ff_1 (.clk(clock_1_out), .D(mux_1_q1_2), .Q(Q3_2));  // open: Qn, preset, en, reset
  D_Flip_Flop d_ff_2 (.clk(clock_1_out), .D(mux_1_q2_2), .Q(Q2_2));  // open: Qn, preset, en, reset
  D_Flip_Flop d_ff_3 (.clk(clock_1_out), .D(mux_1_q3_2), .Q(Q1_2));  // open: Qn, preset, en, reset
endmodule
