// Logisim project mod 6.circ as structural Verilog: 3 circuits, main circuit combo
module combo (
  input  q1,
  input  q2,
  input  q3,
  output s0,
  output s1,
  output s2
);


  assign s0 = q1;
  assign s1 = q2;
  assign s2 = q3;
endmodule

module mux (
  input  q1,
  input  q2,
  input  q3,
  output Q1_2,
  output Q2_2,
  output Q3_2
);

  wire multiplexer_1_out, multiplexer_2_out, multiplexer_3_out, undriven, undriven_2;
  wire [2:0] combo_1_s0;

  combo combo_1 (.q1(q1), .q2(q2), .q3(undriven), .s0(combo_1_s0[0]), .s1(combo_1_s0[1]), .s2(combo_1_s0[2]));
  Multiplexer #(.select(3)) multiplexer_1 (
    .in0(1'b1), .in1(1'b1), .in2(undriven_2), .in3(undriven_2), .in4(undriven_2), .in5(undriven_2),
    .in6(1'b1), .in7(1'b1), .out(multiplexer_1_out), .sel(combo_1_s0));  // open: en
  Multiplexer #(.select(3)) multiplexer_2 (
    .in0(1'b1), .in1(undriven_2), .in2(undriven_2), .in3(undriven_2), .in4(undriven_2), .in5(1'b1),
    .in6(1'b1), .in7(1'b1), .out(multiplexer_2_out), .sel(combo_1_s0));  // open: en
  Multiplexer #(.select(3)) multiplexer_3 (
    .in0(undriven_2), .in1(undriven_2), .in2(undriven_2), .in3(1'b1), .in4(1'b1), .in5(1'b1), .in6(1'b1),
    .in7(undriven_2), .out(multiplexer_3_out), .sel(combo_1_s0));  // open: en
endmodule

module main (
);

  wire d_ff_1_q, d_ff_2_q, d_ff_3_q, mux_1_q1_2, mux_1_q2_2, mux_1_q3_2, undriven;

  mux mux_1 (.q1(d_ff_1_q), .q2(d_ff_2_q), .q3(d_ff_3_q), .Q1_2(mux_1_q1_2), .Q2_2(mux_1_q2_2), .Q3_2(mux_1_q3_2));
  Clock clock_1 ();  // open: out
  D_Flip_Flop d_ff_1 (.clk(undriven), .D(mux_1_q1_2), .Q(d_ff_1_q));  // open: Qn, preset, en, reset
  D_Flip_Flop d_ff_2 (.clk(undriven), .D(mux_1_q2_2), .Q(d_ff_2_q));  // open: Qn, preset, en, reset
  D_Flip_Flop d_ff_3 (.clk(undriven), .D(mux_1_q3_2), .Q(d_ff_3_q));  // open: Qn, preset, en, reset
endmodule
