// Logisim project mod4 ring counter.circ as structural Verilog: 2 circuits, main circuit main
module main (
  input  in_1,
  output out_2,
  output out_3,
  output out_4,
  output out_5
);

  wire clock_1_out, combo_1_da, combo_1_db, combo_1_dc, combo_1_dd, d_ff_3_q, d_ff_4_q, d_ff_5_q, d_ff_6_q;

  D_Flip_Flop d_ff_1 (.clk(in_1), .D(out_5), .Q(out_2));  // open: Qn, preset, en, reset
  Clock clock_1 (.out(clock_1_out));
  combo combo_1 (
    .qa(d_ff_3_q), .qb(d_ff_4_q), .qc(d_ff_5_q), .qd(d_ff_6_q), .da(combo_1_da), .db(combo_1_db),
    .dc(combo_1_dc), .dd(combo_1_dd));
  D_Flip_Flop d_ff_2 (.clk(in_1), .D(out_2), .Q(out_3));  // open: Qn, preset, en, reset
  D_Flip_Flop d_ff_3 (.clk(clock_1_out), .D(combo_1_da), .Q(d_ff_3_q));  // open: Qn, preset, en, reset
  D_Flip_Flop d_ff_4 (.clk(clock_1_out), .D(combo_1_db), .Q(d_ff_4_q));  // open: Qn, preset, en, reset
  D_Flip_Flop d_ff_5 (.clk(clock_1_out), .D(combo_1_dc), .Q(d_ff_5_q));  // open: Qn, preset, en, reset
  D_Flip_Flop d_ff_6 (.clk(clock_1_out), .D(combo_1_dd), .Q(d_ff_6_q));  // open: Qn, preset, en, reset
  D_Flip_Flop d_ff_7 (.clk(in_1), .D(out_3), .Q(out_4));  // open: Qn, preset, en, reset
  D_Flip_Flop d_ff_8 (.clk(in_1), .D(out_4), .Q(out_5));  // open: Qn, preset, en, reset
endmodule

module combo (
  input  qa,
  input  qb,
  input  qc,
  input  qd,
  output da,
  output db,
  output dc,
  output dd
);


  assign da = qd;
  assign db = qa;
  assign dc = qb;
  assign dd = qc;
endmodule
