// Logisim project mod7 twisted ring counter.circ as structural Verilog: 2 circuits, main circuit main
module main (
  input  in_1,
  output out_2,
  output out_3,
  output out_4,
  output out_5
);

  wire and_1_out, clock_1_out, combo_1_da, combo_1_db, combo_1_dc, combo_1_dd, d_ff_3_qn, d_ff_4_q, d_ff_5_q,
       d_ff_6_q, d_ff_7_q, d_ff_8_qn;

  D_Flip_Flop d_ff_1 (.clk(in_1), .D(and_1_out), .Q(out_2));  // open: Qn, preset, en, reset
  D_Flip_Flop d_ff_2 (.clk(in_1), .D(out_2), .Q(out_3));  // open: Qn, preset, en, reset
  Clock clock_1 (.out(clock_1_out));
  combo combo_1 (
    .qa(d_ff_4_q), .qb(d_ff_5_q), .qc(d_ff_6_q), .qd(d_ff_7_q), .da(combo_1_da), .db(combo_1_db),
    .dc(combo_1_dc), .dd(combo_1_dd));
  D_Flip_Flop d_ff_3 (.clk(in_1), .D(out_3), .Q(out_4), .Qn(d_ff_3_qn));  // open: preset, en, reset
  and and_1 (and_1_out, d_ff_3_qn, d_ff_8_qn);
  D_Flip_Flop d_ff_4 (.clk(clock_1_out), .D(combo_1_da), .Q(d_ff_4_q));  // open: Qn, preset, en, reset
  D_Flip_Flop d_ff_5 (.clk(clock_1_out), .D(combo_1_db), .Q(d_ff_5_q));  // open: Qn, preset, en, reset
  D_Flip_Flop d_ff_6 (.clk(clock_1_out), .D(combo_1_dc), .Q(d_ff_6_q));  // open: Qn, preset, en, reset
  D_Flip_Flop d_ff_7 (.clk(clock_1_out), .D(combo_1_dd), .Q(d_ff_7_q));  // open: Qn, preset, en, reset
  D_Flip_Flop d_ff_8 (.clk(in_1), .D(out_4), .Q(out_5), .Qn(d_ff_8_qn));  // open: preset, en, reset
endmodule

module combo (
  input  qa,
  input  qb,
  input  qc,
  input  qd,
  output da,
  output db,
  output dc,
  output dd
);

  wire not_1_out, not_2_out;

  not not_1 (not_1_out, qc);
  and and_1 (da, not_1_out, not_2_out);
  not not_2 (not_2_out, qd);

  assign db = qa;
  assign dc = qb;
  assign dd = qc;
endmodule
