// Logisim project mod8 twisted ring counter muxes.circ as structural Verilog: 3 circuits, main circuit main
module main (
);

  wire clock_1_out, d_ff_1_q, d_ff_2_q, d_ff_3_q, d_ff_4_q, muxes_1_qa_2, muxes_1_qb_2, muxes_1_qc_2,
       muxes_1_qd_2;

  muxes muxes_1 (
    .qa(d_ff_1_q), .qb(d_ff_2_q), .qc(d_ff_3_q), .qd(d_ff_4_q), .Qa_2(muxes_1_qa_2), .Qb_2(muxes_1_qb_2),
    .Qc_2(muxes_1_qc_2), .Qd_2(muxes_1_qd_2));
  Clock clock_1 (.out(clock_1_out));
  D_Flip_Flop d_ff_1 (.clk(clock_1_out), .D(muxes_1_qa_2), .Q(d_ff_1_q));  // open: Qn, preset, en, reset
  D_Flip_Flop d_ff_2 (.clk(clock_1_out), .D(muxes_1_qb_2), .Q(d_ff_2_q));  // open: Qn, preset, en, reset
  D_Flip_Flop d_ff_3 (.clk(clock_1_out), .D(muxes_1_qc_2), .Q(d_ff_3_q));  // open: Qn, preset, en, reset
  D_Flip_Flop d_ff_4 (.clk(clock_1_out), .D(muxes_1_qd_2), .Q(d_ff_4_q));  // open: Qn, preset, en, reset
endmodule

module combo (
  input  qa,
  input  qb,
  input  qc,
  input  qd,
  output s0,
  output s1,
  output s2
);

  wire and_1_out, and_2_out, and_3_out, and_4_out, and_5_out, and_6_out, not_2_out, not_3_out, not_4_out,
       not_5_out, not_6_out, not_7_out;

  not not_1 (s0, qd);
  not not_2 (not_2_out, qb);
  and and_1 (and_1_out, not_2_out, not_3_out);
  not not_3 (not_3_out, qd);
  and and_2 (and_2_out, qb, qd);
  not not_4 (not_4_out, qa);
  and and_3 (and_3_out, not_4_out, not_5_out);
  not not_5 (not_5_out, qd);
  not not_6 (not_6_out, qb);
  and and_4 (and_4_out, not_6_out, qc);
  and and_5 (and_5_out, qb, not_7_out);
  not not_7 (not_7_out, qc);
  and and_6 (and_6_out, qa, qd);
  or or_1 (s1, and_1_out, and_2_out);
  or or_2 (s2, and_3_out, and_4_out, and_5_out, and_6_out);
endmodule

module muxes (
  input  qa,
  input  qb,
  input  qc,
  input  qd,
  output Qa_2,
  output Qb_2,
  output Qc_2,
  output Qd_2
);

  wire [2:0] combo_1_s2;

  combo combo_1 (.qa(qa), .qb(qb), .qc(qc), .qd(qd), .s0(combo_1_s2[2]), .s1(combo_1_s2[1]), .s2(combo_1_s2[0]));
  Multiplexer #(.select(3)) multiplexer_1 (
    .in0(1'b0), .in1(1'b0), .in2(1'b1), .in3(1'b1), .in4(1'b1), .in5(1'b1), .in6(1'b0), .in7(1'b0),
    .out(Qa_2), .sel(combo_1_s2));  // open: en
  Multiplexer #(.select(3)) multiplexer_2 (
    .in0(1'b0), .in1(1'b1), .in2(1'b1), .in3(1'b1), .in4(1'b1), .in5(1'b0), .in6(1'b0), .in7(1'b0),
    .out(Qb_2), .sel(combo_1_s2));  // open: en
  Multiplexer #(.select(3)) multiplexer_3 (
    .in0(1'b1), .in1(1'b1), .in2(1'b1), .in3(1'b1), .in4(1'b0), .in5(1'b0), .in6(1'b0), .in7(1'b0),
    .out(Qc_2), .sel(combo_1_s2));  // open: en
  Multiplexer #(.select(3)) multiplexer_4 (
    .in0(1'b1), .in1(1'b1), .in2(1'b1), .in3(1'b0), .in4(1'b0), .in5(1'b0), .in6(1'b0), .in7(1'b1),
    .out(Qd_2), .sel(combo_1_s2));  // open: en
endmodule
